# Fritzing sketch Light (saved by Fritzing 0.9.9b)
perfboards: 10

parts:
  JP1 = Header 1 [package=1x01_offset]
  JP2 = Header 1 [package=1x01_offset]  # not connected
  Q1 = NPN-Transistor [package="TO92 [THT]"]
  JP3 = Header 1 [package=1x01_offset]  # not connected
  JP4 = Header 1 [package=1x01_offset]
  R1 = Resistor [tolerance=±5% resistance=1M package="1206 [SMD]"]
  R2 = Resistor [tolerance=±5% resistance=1M package="1206 [SMD]"]
  JP5 = Header 1 [package=1x01_offset]
  JP6 = Header 1 [package=1x01_offset]
  Q2 = NPN-Transistor [package="TO92 [THT]"]
  M1 = RioRand LM2596
  M2 = RioRand LM2596
  M3 = RioRand LM2596
  JP7 = Header 1 [package=1x01_offset]
  JP8 = Header 1 [package=1x01_offset]
  A1 = cks pd65W
  Q6 = npn-Powertransistor [package="TO220 [THT]"]
  Q7 = npn-Powertransistor [package="TO220 [THT]"]
  WeMos_D1_Mini_Relay_Shield_V1 = WeMos D1 Mini Relay Shield V2
  WeMos_D1_Mini_Relay_Shield_V2 = WeMos D1 Mini Relay Shield V2
  WeMos_D1_Mini_Relay_Shield_V3 = WeMos D1 Mini Relay Shield V2
  WeMos_D1_Mini_Relay_Shield_V4 = WeMos D1 Mini Relay Shield V2
  J1 = double row male pin header, 6 pins [form="♂ (male)"]
  R3 = Resistor [tolerance=±5% resistance=10k package="0805 [SMD]"]
  R4 = Resistor [tolerance=±5% resistance=10k package="0805 [SMD]"]
  R9 = Resistor [tolerance=±5% resistance=1M package="1206 [SMD]"]  # not connected
  R10 = Resistor [tolerance=±5% resistance=1M package="1206 [SMD]"]
  LED1 = LED - 5mm [color="Red (633nm)" package="5 mm [THT]"]
  LED2 = LED - 5mm [color="Red (633nm)" package="5 mm [THT]"]
  LED3 = LED - 5mm [color="Red (633nm)" package="5 mm [THT]"]
  JP13 = Header 1 [package=1x01_offset]
  JP14 = Header 1 [package=1x01_offset]
  F1 = Resettable Fuse PTC [package=ptc]
  JP15 = Header 1 [package=1x01_offset]
  JP16 = Header 1 [package=1x01_offset]  # not connected
  JP17 = Header 1 [package=1x01_offset]  # not connected
  JP18 = Header 1 [package=1x01_offset]
  JP19 = Header 1 [package=1x01_offset]  # not connected
  Q11 = NPN-Transistor [package="TO92 [THT]"]
  R11 = Resistor [tolerance=±5% resistance=1M package="1206 [SMD]"]
  R12 = Resistor [tolerance=±5% resistance=20k package="1206 [SMD]"]
  R13 = Resistor [tolerance=±5% resistance=20k package="1206 [SMD]"]
  R14 = Resistor [tolerance=±5% resistance=20k package="1206 [SMD]"]
  Part2 = PN532 Elechouse RFID NFC Module V3
  Part3 = HC-SR501 Body Sensor Module
  A2 = weact studio black pill
  Q12 = MOSFET-PCHANNEL-SOIC8 [package=so08]
  Power_plug1 = Power plug
  JP20 = Header 1 [package=1x01_offset]
  JP21 = Header 1 [package=1x01_offset]
  JP23 = Header 1 [package=1x01_offset]
  JP24 = Header 1 [package=1x01_offset]  # not connected
  JP25 = Header 1 [package=1x01_offset]
  JP26 = Header 1 [package=1x01_offset]
  JP27 = Header 1 [package=1x01_offset]
  JP28 = Header 1 [package=1x01_offset]
  JP29 = Header 1 [package=1x01_offset]
  JP30 = Header 1 [package=1x01_offset]
  JP31 = Header 1 [package=1x01_offset]
  JP32 = Header 1 [package=1x01_offset]  # not connected
  JP33 = Header 1 [package=1x01_offset]  # not connected
  JP34 = Header 1 [package=1x01_offset]
  JP35 = Header 1 [package=1x01_offset]
  JP36 = Header 1 [package=1x01_offset]
  JP37 = Header 1 [package=1x01_offset]
  JP38 = Header 1 [package=1x01_offset]
  JP39 = Header 1 [package=1x01_offset]  # not connected
  JP40 = Header 1 [package=1x01_offset]
  JP41 = Header 1 [package=1x01_offset]  # not connected
  R15 = Resistor [tolerance=±5% resistance=5k package="0805 [SMD]"]
  R16 = Resistor [tolerance=±5% resistance=15k package="0805 [SMD]"]
  JP43 = Header 1 [package=1x01_offset]
  JP44 = Header 1 [package=1x01_offset]  # not connected
  JP45 = Header 1 [package=1x01_offset]
  JP46 = Header 1 [package=1x01_offset]  # not connected
  JP47 = Header 1 [package=1x01_offset]
  S2 = Round Pushbutton
  S5 = Toggle Switch [package=THT]
  Part1 = Bluetooth HC-05 Macho  # not connected
  JP48 = Header 1 [package=1x01_offset]  # not connected
  JP49 = Header 1 [package=1x01_offset]
  JP52 = Header 1 [package=1x01_offset]  # not connected
  JP54 = Header 1 [package=1x01_offset]
  JP55 = Header 1 [package=1x01_offset]
  JP56 = Header 1 [package=1x01_offset]
  JP57 = Header 1 [package=1x01_offset]  # not connected
  JP58 = Header 1 [package=1x01_offset]
  JP59 = Header 1 [package=1x01_offset]  # not connected
  R17 = Resistor [tolerance=±5% resistance=10k package="0805 [SMD]"]
  R18 = Resistor [tolerance=±5% resistance=10k package="0805 [SMD]"]
  R19 = Resistor [tolerance=±5% resistance=20k package="1206 [SMD]"]
  J2 = JST-B3P-VH [part_number=JST-B3P-VH package=THT]
  J3 = JST-B3P-VH [part_number=JST-B3P-VH package=THT]
  R20 = Resistor [tolerance=±5% resistance=510 package="0805 [SMD]"]
  C1 = Capacitor Polarized [package=panasonic_c]  # not connected
  R21 = Resistor [tolerance=±5% resistance=5k package="1206 [SMD]"]
  R22 = Resistor [tolerance=±5% resistance=20k package="1206 [SMD]"]
  JP60 = Header 1 [package=1x01_offset]  # not connected
  JP62 = Header 1 [package=1x01_offset]  # not connected

nets:
  N1: JP1.1, JP5.1
  N2: Q1.E, R1.Pin_1
  N3: Q1.C, JP6.1
  N4: JP4.1, Q2.B
  N5: R2.Pin_1, Q2.E
  N6: M1.Pin_1, Q12.D
  N7: M1.Pin_3, WeMos_D1_Mini_Relay_Shield_V2.NC
  N8: M1.Pin_4, M2.Pin_4, M3.Pin_4, JP40.1
  N9: M2.Pin_1, M3.Pin_1
  N10: M2.Pin_3, R3.Pin_0, R4.Pin_0, R12.Pin_0, R13.Pin_0, R14.Pin_0, R19.Pin_0
  N11: M3.Pin_2, JP8.1, Power_plug1.GND
  N12: JP7.1, F1.2, Q12.S
  N13: A1.Pin_1, WeMos_D1_Mini_Relay_Shield_V2.NO, WeMos_D1_Mini_Relay_Shield_V3.NO
  N14: Q6.base, R3.Pin_1, JP35.1, JP38.1, S5.L2
  N15: Q6.emitter, WeMos_D1_Mini_Relay_Shield_V3.COM, LED2.cathode, LED2.anode
  N16: Q7.base, R4.Pin_1, R10.Pin_1, JP36.1
  N17: Q7.emitter, WeMos_D1_Mini_Relay_Shield_V2.COM, LED1.cathode, LED1.anode
  N18: WeMos_D1_Mini_Relay_Shield_V1.COM, JP13.1
  N19: WeMos_D1_Mini_Relay_Shield_V4.COM, J3.pin1
  N20: WeMos_D1_Mini_Relay_Shield_V4.NO, J2.pin1
  N21: J1.pin2, R19.Pin_1
  N22: J1.pin3, R12.Pin_1
  N23: J1.pin4, R13.Pin_1
  N24: J1.pin5, R14.Pin_1
  N25: LED3.cathode, JP14.1
  N26: F1.1, Power_plug1.VCC
  N27: JP15.1, JP58.1
  N28: JP18.1, Q11.B
  N29: Q11.E, R11.Pin_1
  N30: Part2.SCK, Part2.MOSI, JP54.1, JP56.1
  N31: Part2.MISO, JP55.1
  N32: Part3.OUT, JP23.1, JP25.1, JP26.1, JP27.1, JP28.1, JP29.1, JP34.1, S2.leg1
  N33: A2.Pin_14, R15.Pin_1, R16.Pin_0
  N34: A2.Pin_21, JP49.1
  N35: A2.Pin_22, A2.Pin_44, R20.Pin_1
  N36: A2.Pin_23, A2.Pin_43, R15.Pin_0
  N37: A2.Pin_24, A2.Pin_42
  N38: JP20.1, JP21.1, R17.Pin_0, R18.Pin_0
  N39: JP30.1, JP31.1
  N40: JP37.1, S5.L1
  N41: JP43.1, JP47.1, S5.COM, R20.Pin_0
  N42: JP45.1, S2.leg0
  N43: J2.pin2, J3.pin2
  N44: J2.pin3, J3.pin3
  N45: R21.Pin_0, R22.Pin_1

notes:
  buck converters are 8 height not 9
  Use BIG WIRE ->
  |
  v
  Relay Left
  RelayRight
  RelayCenter
  12V red
  7V green
  5V Yellow
  3.3V Orange
  GND
  Headlights
  Horn 1
  Horn 2
  XT60
  Fuse
  LED Strip Lights Data
  Turn Signal Left
  Turn Signal Right
  Brake Light center
  High Power 10A Max
  Low Power 2A max
  White is Antenna
  must be usable
  10k
  3x motion detector
  Headlight
  Horn
  3rd relay brake
  Inputs for: Headlight, Horn, Brake, parking button
  2BLE (A3 A2), Throttle V (A1), none (A0)
  Throttle signal
  FardriverOn_Signal
  Tailight Brightness Signal
  Speedometer
  Throttle V ADC (A1)
  Throttle V Real
  Voltage Divide by 4
  Speedometer IO Pin

custom parts:
  cks pd65W: QC4.0 QC3.0 Type-C USB PD65W Fast Charging Adapter Module DC8-32V 3.25A 65W Step Down Module For Huawei SCP/FCP Apple PD.
  PN532 Elechouse RFID NFC Module V3: NFC is a popular technology in recent years. We often heard this work while smart phone company such as Samsung or HTC introduces their latest high-end phones. Almost all the high-end phone in the market support NFC. Near field communication (NFC) is a set of standards for smart phones and similar devices to establish radio communication with each other by touching them together or bringing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
  HC-SR501 Body Sensor Module: Pyroelectric Infrared PIR Motion Sensor Detector Module
  weact studio black pill: The STM32F401CE based Black Pill V3.0+ Board.
