# Fritzing sketch Light (saved by Fritzing 0.9.9b)
perfboards: 8

parts:
  JP1 = Header 1 [package=1x01_offset]
  JP2 = Header 1 [package=1x01_offset]  # not connected
  Q1 = NPN-Transistor [package="TO92 [THT]"]
  JP3 = Header 1 [package=1x01_offset]  # not connected
  JP4 = Header 1 [package=1x01_offset]
  R1 = Resistor [tolerance=±5% resistance=1M package="1206 [SMD]"]
  R2 = Resistor [tolerance=±5% resistance=1M package="1206 [SMD]"]
  JP5 = Header 1 [package=1x01_offset]
  JP6 = Header 1 [package=1x01_offset]
  Q2 = NPN-Transistor [package="TO92 [THT]"]
  M1 = RioRand LM2596
  M2 = RioRand LM2596
  M3 = RioRand LM2596
  JP7 = Header 1 [package=1x01_offset]
  JP8 = Header 1 [package=1x01_offset]
  A1 = cks pd65W
  Q5 = npn-Powertransistor [package="TO220 [THT]"]
  Q6 = npn-Powertransistor [package="TO220 [THT]"]
  Q7 = npn-Powertransistor [package="TO220 [THT]"]
  WeMos_D1_Mini_Relay_Shield_V1 = WeMos D1 Mini Relay Shield V2
  WeMos_D1_Mini_Relay_Shield_V2 = WeMos D1 Mini Relay Shield V2
  WeMos_D1_Mini_Relay_Shield_V3 = WeMos D1 Mini Relay Shield V2
  WeMos_D1_Mini_Relay_Shield_V4 = WeMos D1 Mini Relay Shield V2  # not connected
  J1 = double row male pin header, 6 pins [form="♂ (male)"]
  R3 = Resistor [tolerance=±5% resistance=1k package="0805 [SMD]"]
  R4 = Resistor [tolerance=±5% resistance=1k package="0805 [SMD]"]
  R5 = Resistor [tolerance=±5% resistance=1k package="0805 [SMD]"]
  R6 = Resistor [tolerance=±5% resistance=1k package="0805 [SMD]"]
  Q8 = npn-Powertransistor [package="TO220 [THT]"]
  R7 = Resistor [tolerance=±5% resistance=1M package="1206 [SMD]"]
  R8 = Resistor [tolerance=±5% resistance=1M package="1206 [SMD]"]
  R9 = Resistor [tolerance=±5% resistance=1M package="1206 [SMD]"]
  R10 = Resistor [tolerance=±5% resistance=1M package="1206 [SMD]"]
  LED1 = LED - 5mm [color="Red (633nm)" package="5 mm [THT]"]
  LED2 = LED - 5mm [color="Red (633nm)" package="5 mm [THT]"]  # not connected
  LED3 = LED - 5mm [color="Red (633nm)" package="5 mm [THT]"]
  JP9 = Header 1 [package=1x01_offset]
  JP10 = Header 1 [package=1x01_offset]
  JP11 = Header 1 [package=1x01_offset]
  JP12 = Header 1 [package=1x01_offset]  # not connected
  JP13 = Header 1 [package=1x01_offset]
  JP14 = Header 1 [package=1x01_offset]
  F1 = Resettable Fuse PTC [package=ptc]
  JP15 = Header 1 [package=1x01_offset]  # not connected
  JP16 = Header 1 [package=1x01_offset]  # not connected
  JP17 = Header 1 [package=1x01_offset]  # not connected
  JP18 = Header 1 [package=1x01_offset]
  JP19 = Header 1 [package=1x01_offset]  # not connected
  Q11 = NPN-Transistor [package="TO92 [THT]"]
  R11 = Resistor [tolerance=±5% resistance=1M package="1206 [SMD]"]
  R12 = Resistor [tolerance=±5% resistance=20k package="1206 [SMD]"]
  R13 = Resistor [tolerance=±5% resistance=20k package="1206 [SMD]"]
  R14 = Resistor [tolerance=±5% resistance=20k package="1206 [SMD]"]
  Part1 = Bluetooth HC-05 Macho  # not connected
  Part2 = PN532 Elechouse RFID NFC Module V3  # not connected
  Part3 = HC-SR501 Body Sensor Module  # not connected
  Part4 = HC-SR501 Body Sensor Module  # not connected
  Part5 = HC-SR501 Body Sensor Module  # not connected
  A2 = weact studio black pill
  Q12 = MOSFET-PCHANNEL-SOIC8 [package=so08]
  Power_plug1 = Power plug

nets:
  N1: JP1.1, JP5.1
  N2: Q1.E, R1.Pin_1
  N3: Q1.C, JP6.1
  N4: JP4.1, Q2.B
  N5: R2.Pin_1, Q2.E
  N6: M1.Pin_1, Q12.D
  N7: M1.Pin_3, Q5.collector, Q6.collector
  N8: M1.Pin_4, M2.Pin_4, M3.Pin_4, JP10.1
  N9: M2.Pin_1, M3.Pin_1
  N10: M2.Pin_3, R3.Pin_0, R4.Pin_0, R5.Pin_0, R6.Pin_0
  N11: M3.Pin_2, JP8.1, Power_plug1.GND
  N12: JP7.1, F1.2, Q12.S
  N13: A1.Pin_1, Q7.collector, Q8.collector, R12.Pin_0, R13.Pin_0, R14.Pin_0
  N14: Q5.base, R5.Pin_1, R8.Pin_1
  N15: Q5.emitter, WeMos_D1_Mini_Relay_Shield_V3.NC
  N16: Q6.base, R3.Pin_1, R9.Pin_1
  N17: Q6.emitter, WeMos_D1_Mini_Relay_Shield_V2.NC
  N18: Q7.base, R4.Pin_1, R10.Pin_1
  N19: Q7.emitter, WeMos_D1_Mini_Relay_Shield_V3.NO
  N20: WeMos_D1_Mini_Relay_Shield_V1.COM, JP13.1
  N21: WeMos_D1_Mini_Relay_Shield_V2.COM, LED1.anode, JP9.1
  N22: WeMos_D1_Mini_Relay_Shield_V2.NO, Q8.emitter
  N23: WeMos_D1_Mini_Relay_Shield_V3.COM, JP11.1
  N24: J1.pin3, R12.Pin_1
  N25: J1.pin4, R13.Pin_1
  N26: J1.pin5, R14.Pin_1
  N27: R6.Pin_1, Q8.base, R7.Pin_1
  N28: LED3.cathode, JP14.1
  N29: F1.1, Power_plug1.VCC
  N30: JP18.1, Q11.B
  N31: Q11.E, R11.Pin_1
  N32: A2.Pin_22, A2.Pin_44
  N33: A2.Pin_23, A2.Pin_43
  N34: A2.Pin_24, A2.Pin_42

notes:
  buck converters are 8 height not 9
  Use BIG WIRE ->
  |
  v
  Relay Left
  RelayRight
  RelayCenter
  12V red
  7V green
  5V Yellow
  3.3V Orange
  GND
  Headlights
  Horn 1
  Horn 2
  XT60
  Fuse
  LED Strip Lights Data
  Relay is not on a perf board. connection into it are screw terminal except for the JST.
  Can be improvised
  Turn Signal Left
  Turn Signal Right
  Brake Light center
  High Power 10A Max
  Low Power 2A max
  White is Antenna
  must be usable
  TODO: ADC12V, ADC Throttle

custom parts:
  cks pd65W: QC4.0 QC3.0 Type-C USB PD65W Fast Charging Adapter Module DC8-32V 3.25A 65W Step Down Module For Huawei SCP/FCP Apple PD.
  PN532 Elechouse RFID NFC Module V3: NFC is a popular technology in recent years. We often heard this work while smart phone company such as Samsung or HTC introduces their latest high-end phones. Almost all the high-end phone in the market support NFC. Near field communication (NFC) is a set of standards for smart phones and similar devices to establish radio communication with each other by touching them together or bringing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
  HC-SR501 Body Sensor Module: Pyroelectric Infrared PIR Motion Sensor Detector Module
  weact studio black pill: The STM32F401CE based Black Pill V3.0+ Board.
